// Digital circuit BW8cpu.dig as structural Verilog
module BW8cpu (
  input  VCC,
  input  GND,
  input  nIRQ,
  input  nREQ,
  input  crystal,
  input  _555,
  input  step,
  input  [7:0] Memory,
  output [15:0] ADDR,
  output R_nW,
  output nACK,
  output nBRK
);

  wire a_dbus_a, a_dbus_l, addr_a, alu_dbus_a, alu_op, alu_res, b_dbus_a, b_dbus_l, c_dbus_a, c_dbus_l, clk,
       clk_crystal, count, d_dbus_a, d_dbus_l, dbus_a, dbus_l, dec_sp, dp_dbus_a, dp_dbus_l, dpi_dbus_a, ext,
       ir_dbus_l, isr_xfer_a, lhs, mem_dbus_a, mem_dbus_l, nclk, nirq_latched, nrst, nRST_out, pc_addr_a,
       pc_inc, pc_xfer_a, pc_xfer_l, reg_a, reg_b, reg_c, reg_d, reg_dp, reg_pc, reg_sp, reg_t1, reg_t2,
       reg_x, reg_y, rhs, rst, rst_latched, rst_xfer_a, sp_addr_a, sp_dec, sp_inc, sp_xfer_a, sp_xfer_l,
       spi_xfer_a, sr_dbus_a, sr_dbus_l, t1_dbus_a, t2_dbus_a, x_addr_a, x_dec, x_inc, x_xfer_a, x_xfer_l,
       xfer_a, xfer_l, y_addr_a, y_dec, y_inc, y_xfer_a, y_xfer_l, zero_dbus_a;
  wire [2:0] Break_out, t_state, triple_clock_1_p9;
  wire [4:0] flags;
  wire [7:0] dbus, opcode;
  wire [15:0] xfer;

  // Probe on dbus
  // Probe on xfer
  // Probe on ADDR
  // Probe on Memory
  // Probe on reg_a
  // Probe on reg_b
  // Probe on reg_c
  // Probe on reg_d
  // Probe on reg_dp
  // Probe on reg_t2
  // Probe on alu_res
  PowerSupply powersupply_1 (.VDD(VCC), .GND(GND));
  // Probe on reg_pc
  // Probe on reg_sp
  // Probe on reg_x
  // Probe on reg_y
  // Probe on reg_t1
  // Probe on rst_latched
  // Probe on nirq_latched
  // Probe on opcode
  // Probe on ext
  // Probe on flags
  // control_unit Control_Unit: pin names not known; wires that end beside it: nIRQ, opcode, flags, nREQ, clk, nrst, dbus_a, dbus_l, alu_op, xfer_a, xfer_l, addr_a, count, dec_sp, nBRK, nclk, rst, {rst_latched, nirq_latched, ext, opcode, flags, t_state}
  instruction_register Instruction_Register (
    .clk(clk), .dbus(dbus), .dbus_load(ir_dbus_l), .clr(nrst), .opcode(opcode));
  constant_generator_8bit DP_Initial_Val (
    .dpi_dbus_assert(dpi_dbus_a), .DPi(8'h1), .zero_dbus_assert(zero_dbus_a), .dbus(dbus));
  memory_bridge Memory_Bridge (.dbus_assert(mem_dbus_a), .dbus_load(mem_dbus_l), .dbus(dbus), .mbus(Memory));
  reset_module reset_module_1 (.clk(clk_crystal), .nrst_in(nRST_out), .nrst(nrst));
  Button u_nRST (.out(nRST_out));
  Button #(.activeLow("true")) Run (.out(Break_out[0]));
  Button #(.activeLow("true")) Demo (.out(Break_out[1]));
  Button #(.activeLow("true")) Break (.out(Break_out[2]));
  // Probe on t_state
  // triple_clock triple_clock_1: pin names not known; wires that end beside it: Break_out, nBRK, {nrst, 2'b11}, crystal, _555, step, clk, clk_crystal, triple_clock_1_p9
  // Probe on rst
  // Probe on nclk
  LED u_crystal (.in(clk_crystal));
  // Probe on dec_sp
  // Probe on nBRK
  LED cpu (.in(clk));
  LED Run_Mode_Active (.in(triple_clock_1_p9[0]));
  LED Demo_Mode_Active (.in(triple_clock_1_p9[1]));
  LED Break_Mode_Active (.in(triple_clock_1_p9[2]));
  // Probe on count
  // Probe on addr_a
  // Probe on xfer_l
  // Probe on xfer_a
  // bus_controller Bus_Controller: pin names not known; wires that end beside it: dbus_a, dbus_l, xfer_a, xfer_l, addr_a, clk, count, dec_sp, nclk, alu_dbus_a, a_dbus_a, b_dbus_a, c_dbus_a, d_dbus_a, sr_dbus_a, dp_dbus_a, t1_dbus_a, t2_dbus_a, mem_dbus_l, a_dbus_l, b_dbus_l, c_dbus_l, d_dbus_l, sr_dbus_l, dp_dbus_l
  // Probe on alu_op
  // Probe on dbus_l
  // Probe on dbus_a
  // alu Arithmetic___Logic_Unit_and_Status_Register: pin names not known; wires that end beside it: alu_op, sr_dbus_l, sr_dbus_a, clk, rst, lhs, rhs, alu_dbus_a, flags, dbus, alu_res
  gpr_pair A_and_B ();  // open: naddr_assert, nxfer_load, nhi_dbus_load, nlo_dbus_load, nhi_dbus_assert, nlo_dbus_assert, nhi_lhs_assert, nlo_lhs_assert, nhi_rhs_assert, nlo_rhs_assert, dbus, xfer, nclr, addr, reg_hi, reg_lo
  gpr_pair C_and_D ();  // open: naddr_assert, nxfer_load, nhi_dbus_load, nlo_dbus_load, nhi_dbus_assert, nlo_dbus_assert, nhi_lhs_assert, nlo_lhs_assert, nhi_rhs_assert, nlo_rhs_assert, dbus, xfer, nclr, addr, reg_hi, reg_lo
  gpr_pair DP_and_DA ();  // open: naddr_assert, nxfer_load, nhi_dbus_load, nlo_dbus_load, nhi_dbus_assert, nlo_dbus_assert, nhi_lhs_assert, nlo_lhs_assert, nhi_rhs_assert, nlo_rhs_assert, dbus, xfer, nclr, addr, reg_hi, reg_lo
  gpr_pair TH_and_TL ();  // open: naddr_assert, nxfer_load, nhi_dbus_load, nlo_dbus_load, nhi_dbus_assert, nlo_dbus_assert, nhi_lhs_assert, nlo_lhs_assert, nhi_rhs_assert, nlo_rhs_assert, dbus, xfer, nclr, addr, reg_hi, reg_lo
  // address_register Program_Counter: pin names not known; wires that end beside it: xfer, rst, pc_xfer_l, pc_addr_a, pc_xfer_a, pc_inc, 1'b1, clk, ADDR, reg_pc
  // address_register Stack_Pointer: pin names not known; wires that end beside it: xfer, rst, sp_xfer_l, sp_addr_a, sp_xfer_a, sp_inc, sp_dec, clk, ADDR, reg_sp
  // address_register X_Index: pin names not known; wires that end beside it: xfer, rst, x_xfer_l, x_addr_a, x_xfer_a, x_inc, x_dec, clk, ADDR, reg_x
  // address_register Y_Index: pin names not known; wires that end beside it: xfer, rst, y_xfer_l, y_addr_a, y_xfer_a, y_inc, y_dec, clk, ADDR, reg_y
  constant_generator_16bit RST_Vector_Hi__ISR_Vector_Hi__and_SP_Init_Val (
    .RSTv_Lo(16'h100), .ISRv_Lo(16'hfe), .SPi(16'h7fff), .SPi_xfer_assert(spi_xfer_a),
    .RST_xfer_assert(rst_xfer_a), .ISR_xfer_assert(isr_xfer_a), .xfer(xfer));

  assign R_nW = 1'b0;

  // Other names for the same wires on the sheet: ack_addr_a = nACK; clk_cpu = clk; mbus[7:0] = Memory;
  //   rst_clk_mode[2] = nrst

  // Notes on the sheet:
  //   VCC: default 1
  //   nIRQ: default 1
  //   nREQ: default 1
  //   crystal: Hz: 5
  //   External Pinout
  //   Buses & Constants
  //   Registers
endmodule
