// Digital circuit control_unit.dig as structural Verilog
module control_unit (
  input  nirq,
  input  [7:0] opcode,
  input  [4:0] flags,
  input  nreq,
  input  clk,
  input  nrst,
  output [3:0] dbus_assert,
  output [4:0] dbus_load,
  output [3:0] alu_op,
  output [4:0] xfer_assert,
  output [2:0] xfer_load,
  output [2:0] addr_assert,
  output [2:0] count,
  output dec_sp,
  output nbrk,
  output nclk,
  output noffset,
  output rst,
  output [17:0] dbg
);

  wire brk, clk_inverter_p5, clk_inverter_p6, m_tog, nirq_latch, offset, or_1_out, rst_useq, sequencer_p1,
       sequencer_p4, sequencer_p5, sequencer_p6;
  wire [7:0] State_Latch_q, ucode0_d, ucode1_d, ucode2_d, ucode3_d;

  // _7404 clk_inverter: pin names not known; wires that end beside it: clk, nrst, brk, offset, clk_inverter_p5, clk_inverter_p6, 1'b1, 1'b0, nclk, rst, nbrk, noffset
  // NotConnected on clk_inverter_p5
  // NotConnected on clk_inverter_p6
  _74ls273 State_Latch (
    .CP(nclk), .nMR(nrst), .D({4'b0000, nirq, 3'b000}), .VCC(1'b1), .GND(1'b0),
    .Q({State_Latch_q[7:4], nirq_latch, State_Latch_q[2:0]}));
  or or_1 (or_1_out, rst_useq, rst);
  // _74193 sequencer: pin names not known; wires that end beside it: sequencer_p1, 1'b1, nclk, sequencer_p4, sequencer_p5, sequencer_p6, or_1_out, 1'b1, 1'b1, 1'b0, dbg[0], dbg[1], dbg[2]
  // NotConnected on sequencer_p1
  // NotConnected on sequencer_p4
  // NotConnected on sequencer_p5
  // NotConnected on sequencer_p6
  ROM #(.AddrBits(18), .Bits(8)) ucode0 (.A({3'b000, opcode, flags[3:0], dbg[2:0]}), .sel(1'b1), .D(ucode0_d));
  ROM #(.AddrBits(18), .Bits(8)) ucode1 (.A({3'b000, opcode, flags[3:0], dbg[2:0]}), .sel(1'b1), .D(ucode1_d));
  ROM #(.AddrBits(18), .Bits(8)) ucode2 (.A({3'b000, opcode, flags[3:0], dbg[2:0]}), .sel(1'b1), .D(ucode2_d));
  ROM #(.AddrBits(18), .Bits(8)) ucode3 (.A({3'b000, opcode, flags[3:0], dbg[2:0]}), .sel(1'b1), .D(ucode3_d));
  _74ls273 _74ls273_1 (.CP(clk), .nMR(nrst), .D(ucode0_d), .VCC(1'b1), .GND(1'b0), .Q({dbus_load[3:0], dbus_assert}));
  _74ls273 _74ls273_2 (
    .CP(clk), .nMR(nrst), .D(ucode1_d), .VCC(1'b1), .GND(1'b0), .Q({xfer_assert[2:0], alu_op, dbus_load[4]}));
  _74ls273 _74ls273_3 (
    .CP(clk), .nMR(nrst), .D(ucode2_d), .VCC(1'b1), .GND(1'b0), .Q({addr_assert, xfer_load, xfer_assert[4:3]}));
  _74ls273 _74ls273_4 (
    .CP(clk), .nMR(nrst), .D(ucode3_d), .VCC(1'b1), .GND(1'b0),
    .Q({brk, offset, m_tog, rst_useq, dec_sp, count}));

  assign dbg[17:3] = {3'b000, opcode, flags[3:0]};

  // Other names for the same wires on the sheet: t_state[2:0] = dbg[2:0];
  //   ucode_addr[14:0] = {opcode, flags[3:0], dbg[2:0]}; C_f = flags[0]; Z_f = flags[1]; V_f = flags[2];
  //   N_f = flags[3]; I_f = flags[4]

  // Notes on the sheet:
  //   ucode0 loads minimal_microcode0.bin
  //   ucode1 loads minimal_microcode1.bin
  //   ucode2 loads minimal_microcode2.bin
  //   ucode3 loads minimal_microcode3.bin
endmodule
